# Fritzing sketch circuit (saved by Fritzing 0.9.3b)

parts:
  WeMos_D1_Mini1 = WeMos D1 Mini
  VCC1 = 4 x AAA Battery Mount
  AM2302_DHT22 = AM2302 DHT22 Humidity and Temperature Sensor

nets:
  3V3: WeMos_D1_Mini1.3V3, AM2302_DHT22.VCC
  N1: WeMos_D1_Mini1.5V, VCC1.+
  N2: WeMos_D1_Mini1.D0, WeMos_D1_Mini1.RST
  N3: WeMos_D1_Mini1.D7, AM2302_DHT22.DAT
  N4: WeMos_D1_Mini1.G, VCC1.-, AM2302_DHT22.GND
